// Logisim project Project2Given.circ as structural Verilog: 4 circuits, main circuit main
module main (
);

  wire and_1_out, and_2_out, B0, B1, B2, B3, B4, B5, B6, B7, B8, B9, BL, BU, C0, C1, C2, CLK, IB1_p6, L1_l,
       L1_u, or_8_out, P1_v, R0, R1, R3, R4, Valid;
  wire [2:0] counter_1_q;
  wire [3:0] IB1_p7, P1_b0, register_3_q, register_4_q, register_5_q;

  Button n1 (.out(B1));
  Button n4 (.out(B4));
  Button n7 (.out(B7));
  Button L (.out(BL));
  Button n3 (.out(B3));
  Button n2 (.out(B2));
  Button n6 (.out(B6));
  Button n5 (.out(B5));
  Button n9 (.out(B9));
  Button n8 (.out(B8));
  Button U (.out(BU));
  Button n0 (.out(B0));
  or or_1 (R0, B3, B2, B1);
  or or_2 (R1, B6, B5, B4);
  or or_3 (R3, B9, B8, B7);
  or or_4 (R4, BU, B0, BL);
  or or_5 (C0, B1, B4, B7, BL);
  or or_6 (C1, B2, B5, B8, B0);
  or or_7 (C2, B3, B6, B9, BU);
  Clock clock_1 (.out(CLK));
  nand nand_1 (Valid, IB1_p7[0], IB1_p7[1], IB1_p7[2], IB1_p7[3]);
  // Probe on P1_b0
  Panel P1 (
    .R0(R0), .R1(R1), .R2(R3), .R3(R4), .C0(C0), .C1(C1), .C2(C2), .B0(P1_b0[0]), .B1(P1_b0[1]),
    .B2(P1_b0[2]), .B3(P1_b0[3]), .V(P1_v));
  LED Press (.in(P1_v));
  // Probe on IB1_p7
  // InputBuffer IB1: pin names not known; wires that end beside it: P1_b0[0], P1_b0[1], P1_b0[2], P1_b0[3], P1_v, IB1_p6, IB1_p7[0], IB1_p7[1], IB1_p7[2], IB1_p7[3]
  not not_1 (IB1_p6, CLK);
  Register #(.width(4)) register_1 (.D(register_3_q), .en(Valid), .clk(CLK));  // open: Q, clr
  Lock L1 (.C0(IB1_p7[0]), .C1(IB1_p7[1]), .C2(IB1_p7[2]), .C3(IB1_p7[3]), .CLK(CLK), .L(L1_l), .U(L1_u));
  Counter #(.max('h7), .width(3)) counter_1 (
    .count(or_8_out), .Q(counter_1_q), .up(L1_u), .clk(CLK));  // open: load, D, carry, clr
  or or_8 (or_8_out, L1_l, L1_u);
  Register #(.width(4)) register_2 (.D(register_3_q), .en(Valid), .clk(CLK));  // open: Q, clr
  LED Unlocked (.in(and_1_out));
  and and_1 (and_1_out, ~counter_1_q[0], ~counter_1_q[1], ~counter_1_q[2]);  // AND_Gate
  Register #(.width(4)) register_3 (.D(register_4_q), .en(Valid), .clk(CLK), .Q(register_3_q));  // open: clr
  LED Locked (.in(and_2_out));
  and and_2 (and_2_out, ~counter_1_q[0], ~counter_1_q[1], counter_1_q[2]);  // AND_Gate
  Register #(.width(4)) register_4 (.D(register_5_q), .en(Valid), .clk(CLK), .Q(register_4_q));  // open: clr
  Register #(.width(4)) register_5 (.D(IB1_p7), .en(Valid), .clk(CLK), .Q(register_5_q));  // open: clr
endmodule

module Panel (
  input  R0,
  input  R1,
  input  R2,
  input  R3,
  input  C0,
  input  C1,
  input  C2,
  output B0,
  output B1,
  output B2,
  output B3,
  output V
);

  wire L_out, n0_out, n1_out, n2_out, n3_out, n4_out, n5_out, n6_out, n7_out, n8_out, n9_out, U_out;

  and n1 (n1_out, R0, C0);
  and n2 (n2_out, R0, C1);
  and n3 (n3_out, R0, C2);
  and n4 (n4_out, R1, C0);
  and n5 (n5_out, R1, C1);
  and n6 (n6_out, R1, C2);
  and n7 (n7_out, R2, C0);
  and n8 (n8_out, R2, C1);
  and n9 (n9_out, R2, C2);
  and L (L_out, R3, C0);
  and n0 (n0_out, R3, C1);
  and U (U_out, R3, C2);
  ExactlyOne xor_1 (.out(B0), .in0(n1_out), .in1(n3_out), .in2(n5_out), .in3(n7_out), .in4(n9_out), .in5(U_out));
  ExactlyOne xor_2 (
    .out(B1), .in0(n2_out), .in1(n3_out), .in2(n5_out), .in3(U_out), .in4(n6_out), .in5(n7_out), .in6(L_out));
  ExactlyOne xor_3 (.out(B2), .in0(n4_out), .in1(n5_out), .in2(n6_out), .in3(n7_out));
  ExactlyOne xor_4 (.out(B3), .in0(n8_out), .in1(n9_out), .in2(L_out), .in3(U_out));
  ExactlyOne xor_5 (
    .out(V), .in0(n1_out), .in1(n2_out), .in2(n3_out), .in3(n4_out), .in4(n5_out), .in5(n6_out),
    .in6(n7_out), .in7(n8_out), .in8(n9_out), .in9(L_out), .in10(n0_out), .in11(U_out));
endmodule

module InputBuffer (
  input  in_1,
  input  B0,
  input  in_3,
  input  B1,
  input  B2,
  input  in_6,
  input  B3,
  input  in_8,
  input  V,
  input  CLK,
  output C0,
  output C1,
  output C2,
  output C3
);

  wire and_1_out, and_2_out, and_3_out, d_ff_1_qn, d_ff_2_q, d_ff_2_qn, NO_S, or_1_out;

  Multiplexer multiplexer_1 (.in0(in_1), .in1(B0), .out(C0), .sel(NO_S));
  Multiplexer multiplexer_2 (.in0(in_3), .in1(B1), .out(C1), .sel(NO_S));
  Multiplexer multiplexer_3 (.in0(in_6), .in1(B2), .out(C2), .sel(NO_S));
  Multiplexer multiplexer_4 (.in0(in_8), .in1(B3), .out(C3), .sel(NO_S));
  and and_1 (and_1_out, NO_S, V);
  and and_2 (and_2_out, d_ff_2_q, V);
  or or_1 (or_1_out, and_1_out, and_2_out);
  and and_3 (and_3_out, d_ff_1_qn, V, d_ff_2_qn);
  D_Flip_Flop d_ff_1 (.D(or_1_out), .clk(CLK), .Q(NO_S), .Qn(d_ff_1_qn));  // open: preset, reset
  D_Flip_Flop d_ff_2 (.D(and_3_out), .clk(CLK), .Q(d_ff_2_q), .Qn(d_ff_2_qn));  // open: preset, reset
endmodule

module Lock (
  input  C0,
  input  C1,
  input  C2,
  input  C3,
  input  CLK,
  output L,
  output U
);

  D_Flip_Flop d_ff_1 ();  // open: D, clk, Q, Qn, preset, reset
  D_Flip_Flop d_ff_2 ();  // open: D, clk, Q, Qn, preset, reset
endmodule
